# Fritzing sketch XJ-LegoBot (saved by Fritzing 0.9.4)
circuit board: 9.3696cm x 5.78335cm

parts:
  Motor_A = DC Motor
  L298N = L298
  Motor_B = DC Motor
  9V = BC9VPC [package=bc9vpc]
  Arduino_UNO = Arduino Uno (Rev3)
  HC-SR04_Sensor_2 = HC-SR04 Ultrasonic Distance Sensor
  HC-SR04_Sensor_3 = HC-SR04 Ultrasonic Distance Sensor

nets:
  N1: Motor_A.pin_1, L298N.Motor_A_1
  N2: Motor_A.pin_2, L298N.Motor_A_2
  5V: L298N.+5V, Arduino_UNO.5V, HC-SR04_Sensor_2.VCC, HC-SR04_Sensor_3.VCC
  GND: L298N.Gnd, 9V.V-, Arduino_UNO.GND, HC-SR04_Sensor_2.GND, HC-SR04_Sensor_3.GND
  N3: L298N.Input_1, Arduino_UNO.D8
  N4: L298N.Input_2, Arduino_UNO.D7
  N5: L298N.Input_3, Arduino_UNO.D12/MISO
  N6: L298N.Input_4, Arduino_UNO.D13/SCK
  N7: L298N.Enable_A, Arduino_UNO.D3_PWM
  N8: L298N.Enable_B, Arduino_UNO.D5_PWM
  N9: L298N.Motor_B_1, Motor_B.pin_1
  N10: L298N.VMS, 9V.V+
  N11: L298N.Motor_B_2, Motor_B.pin_2
  N12: Arduino_UNO.D9_PWM, HC-SR04_Sensor_3.ECHO
  N13: Arduino_UNO.D2, HC-SR04_Sensor_3.TRIG
  N14: Arduino_UNO.D4, HC-SR04_Sensor_2.TRIG
  N15: Arduino_UNO.D6_PWM, HC-SR04_Sensor_2.ECHO

notes:
  El robot del Jordi i del Xavi, Construcció d'un petit robot per practicar els coneixements obtinguts a les classes de robòtica., 1.0

custom parts:
  L298: L298 module
  HC-SR04 Ultrasonic Distance Sensor: The HC-SR04 is an ultrasonic distance sensor. It is capable of providing measurement for ranges of 2cm to 400cm. The module operates at 5V.

// code stored in the sketch: LegoBot_FuncionsMotor.ino
/* Funcions dels motors */

//Atura els dos motors. Para el vehicle.
void aturar() {
  AturarMotorA();
  AturarMotorB();
}

//Atura el motor A.
void AturarMotorA() {
  analogWrite(mAVelocitat, 0);
  digitalWrite(mAEndavant, LOW);
  digitalWrite(mAEnrere, LOW);
}

//Atura el motor B.
void AturarMotorB() {
  analogWrite(mBVelocitat, 0);
  digitalWrite(mBEndavant, LOW);
  digitalWrite(mBEnrere, LOW);
}

//Posa en marxa els dos motors i fa anar el vehicle endavant a la velocitat indicada.
void anarEndavant(int velocitat) {
  anarEndavantA(velocitat);
  anarEndavantB(velocitat);
}

//Posa en marxa el motor A endavant a la velocitat indicada.
void anarEndavantA(int velocitat) {
  digitalWrite(mAEndavant, HIGH);
  digitalWrite(mAEnrere, LOW);
  analogWrite(mAVelocitat, velocitat);
}

//Posa en marxa el motor B endavant a la velocitat indicada.
void anarEndavantB(int velocitat) {
  digitalWrite(mBEndavant, HIGH);
  digitalWrite(mBEnrere, LOW);
  analogWrite(mBVelocitat, velocitat);
}

//Posa en marxa els dos motors i fa anar el vehicle enrere a la velocitat indicada.
void anarEnrere(int velocitat) {
  anarEnrereA(velocitat);
  anarEnrereB(velocitat);
}

//Posa en marxa el motor A enrere a la velocitat indicada.
void anarEnrereA(int velocitat) {
  digitalWrite(mAEndavant, LOW);
  digitalWrite(mAEnrere, HIGH);
  analogWrite(mAVelocitat, velocitat);
}

//Posa en marxa el motor B enrere a la velocitat indicada.
void anarEnrereB(int velocitat) {
  digitalWrite(mBEndavant, LOW);
  digitalWrite(mBEnrere, HIGH);
  analogWrite(mBVelocitat, velocitat);
}

//Posa en marxa els dos motors i fa anar el vehicle endavant, accelerant el vehícle poc a poc fins a la velocitat màxima.
void accelerarEndavant() {
  for (byte i = VELOCITAT_MIN; i < VELOCITAT_MAX; i++) {
    anarEndavant(i);
  }
}

//Posa en marxa els dos motors i fa anar el vehicle enrere, accelerant el vehícle poc a poc fins a la velocitat màxima.
void accelerarEnrere() {
  for (byte i = VELOCITAT_MIN; i < VELOCITAT_MAX; i++) {
    anarEnrere(i);
  }
}

// code stored in the sketch: LegoBot_FuncionsRadar.ino
/* Funcions de control dels radars*/

void llegirRadarDavant () {
  distDavant = radar[0].ping_cm();  
}

void llegirRadarDarrere () {
  distDavant = radar[1].ping_cm();  
}

void llegirRadars () {
  llegirRadarDavant();
  delay(50);
  llegirRadarDarrere();
}

// code stored in the sketch: TestMotor.ino
/* Test del circuit dels motors del XJ-LegoBot
Funcions disponibles:
  anarEndavant(velocitat): Posa en marxa els dos motors i fa anar el vehicle endavant a la velocitat indicada.
  anarEnrere(velocitat): Posa en marxa els dos motors i fa anar el vehicle enrere a la velocitat indicada.
  aturar(): Atura els dos motors. Para el vehicle.

  AturarMotorA(): Atura el motor A.
  AturarMotorB(): Atuea el motor B.
  anarEndavantA(velocitat): Posa en marxa el motor A endavant a la velocitat indicada.
  anarEndavantB(velocitat): Posa en marxa el motor B endavant a la velocitat indicada.
  anarEnrereA(velocitat): Posa en marxa el motor A enrere a la velocitat indicada.
  anarEnrereA(velocitat): Posa en marxa el motor B enrere a la velocitat indicada.
*/

int mAVelocitat =     3;
int mAEndavant =      7;
int mAEnrere =        8;

int mBVelocitat =     5;
int mBEndavant =      12;
int mBEnrere =        13;

int pausa =           1000;
int velocitatMotor =  255;


void setup() {
  pinMode(mAVelocitat,  OUTPUT);
  pinMode(mAEndavant,   OUTPUT);
  pinMode(mAEnrere,     OUTPUT);
  
  pinMode(mBVelocitat,  OUTPUT);
  pinMode(mBEndavant,   OUTPUT);
  pinMode(mBEnrere,     OUTPUT);

}

void loop() {
  //Motors endavant
  anarEndavant(velocitatMotor);
  aturaPausa();
  //Motors enrere
  anarEnrere(velocitatMotor);
  aturaPausa();
  //Motor A endavant. Motor B aturat
  anarEndavantA(velocitatMotor);
  aturaPausa();
  //Motor A endavant. Motor B enrere
  anarEndavantA(velocitatMotor);
  anarEnrereB(velocitatMotor);
  aturaPausa();
  //Motor A aturat. Motor B endavant
  anarEndavantB(velocitatMotor);
  aturaPausa();
  //Motor A enrere. Motor B endavant
  anarEnrereA(velocitatMotor);
  anarEndavantB(velocitatMotor);
  aturaPausa();
}

/* Funcions dels motors */
//Parar el vehicle
void aturar() {
  AturarMotorA();
  AturarMotorB();
}

void aturaPausa() {
  delay(pausa);
  aturar();
  delay(pausa);
}

void AturarMotorA() {
  analogWrite(mAVelocitat, 0);
  digitalWrite(mAEndavant, LOW);
  digitalWrite(mAEnrere, LOW);
}

void AturarMotorB() {
  analogWrite(mBVelocitat, 0);
  digitalWrite(mBEndavant, LOW);
  digitalWrite(mBEnrere, LOW);
}

//Marxa endavant
void anarEndavant(int velocitat) {
  anarEndavantA(velocitat);
  anarEndavantB(velocitat);
}

void anarEndavantA(int velocitat) {
  digitalWrite(mAEndavant, HIGH);
  digitalWrite(mAEnrere, LOW);
  analogWrite(mAVelocitat, velocitat);
}

void anarEndavantB(int velocitat) {
  digitalWrite(mBEndavant, HIGH);
  digitalWrite(mBEnrere, LOW);
  analogWrite(mBVelocitat, velocitat);
}

//Marxa enrere
void anarEnrere(int velocitat) {
  anarEnrereA(velocitat);
  anarEnrereB(velocitat);
}

void anarEnrereA(int velocitat) {
  digitalWrite(mAEndavant, LOW);
  digitalWrite(mAEnrere, HIGH);
  analogWrite(mAVelocitat, velocitat);
}

void anarEnrereB(int velocitat) {
  digitalWrite(mBEndavant, LOW);
  digitalWrite(mBEnrere, HIGH);
  analogWrite(mBVelocitat, velocitat);
}

// code stored in the sketch: XJ-LegoBot.ino
/* Control del XJ-LegoBot
Funcions disponibles:
  anarEndavant(velocitat): Posa en marxa els dos motors i fa anar el vehicle endavant a la velocitat indicada.
  anarEnrere(velocitat): Posa en marxa els dos motors i fa anar el vehicle enrere a la velocitat indicada.
  accelerarEndavant(): Posa en marxa els dos motors i fa anar el vehicle endavant, accelerant el vehícle poc a poc fins a la velocitat màxima.
  accelerarEnrere(): Posa en marxa els dos motors i fa anar el vehicle enrere, accelerant el vehícle poc a poc fins a la velocitat màxima.
  aturar(): Atura els dos motors. Para el vehicle.
  aturarMotorA(): Atura el motor A.
  aturarMotorB(): Atura el motor B.
  anarEndavantA(velocitat): Posa en marxa el motor A endavant a la velocitat indicada.
  anarEndavantB(velocitat): Posa en marxa el motor B endavant a la velocitat indicada.
  anarEnrereA(velocitat): Posa en marxa el motor A enrere a la velocitat indicada.
  anarEnrereB(velocitat): Posa en marxa el motor B enrere a la velocitat indicada.

  llegirRadarDavant(): Llegeix la distància al objecte detectat pel radar davanter a la variable distDavant. Si no detecta res retorna 0.
  llegirRadarDarrere(): Llegeix la distància al objecte detectat per radar del darrere a la variable distDarrere. Si no detecta res retorna 0.
  llegirRadars(): Retorna la lectura de distància de tots els radars a les seves variables.
*/
#include <NewPing.h> //Llibreria de control dels sensors ultrasònics.

#define NUM_RADAR           2   // Nombre de radars utilitzats.
#define DISTANCIA_MAX_RADAR 10  // Distància màxima de detecció en cm per cada radar.

#define VELOCITAT_MAX 255 //Velocitat màxima dels motors
#define VELOCITAT_MIN 150 //Velocitat mínima dels motors

int distDavant =      0;  //Distància a la que es troba un objecte del radar davanter.
int distDarrere =     0;  //Distància a la que es troba un objecte del radar del darrere.

int mAVelocitat =     3;
int mAEndavant =      7;
int mAEnrere =        8;

int mBVelocitat =     5;
int mBEndavant =      12;
int mBEnrere =        13;

/* Definició dels radars.
      radar[0]: radar frontal.
      radar[1]: radar del darrere.
 */
NewPing radar[NUM_RADAR] = {   // Definició de les instàncies dels radars instal.lats.
  NewPing(4, 10, DISTANCIA_MAX_RADAR), // Per cada radar s'ha de definir el pin de trigger, el d'echo i la distància màxima de detecció.
  NewPing(2, 9, DISTANCIA_MAX_RADAR)
};

void setup() {
  pinMode(mAVelocitat,  OUTPUT);
  pinMode(mAEndavant,   OUTPUT);
  pinMode(mAEnrere,     OUTPUT);
  
  pinMode(mBVelocitat,  OUTPUT);
  pinMode(mBEndavant,   OUTPUT);
  pinMode(mBEnrere,     OUTPUT);

  accelerarEndavant();
}

void loop() {
  
}
